# Fritzing sketch shield (saved by Fritzing 0.9.3b)
perfboards: 1

parts:
  Part1 = Arduino Uno (Rev3) - ICSP  # not connected
  J2 = female pin header, 5 pins [form="♀ (female)"]
  J3 = female pin header, 5 pins [form="♀ (female)"]
  J4 = female pin header, 5 pins [form="♀ (female)"]
  J5 = Screw terminal - 2 pins [package=THT]  # not connected

nets:
  N1: J2.pin1, J4.pin1
  N2: J2.pin4, J3.pin4, J4.pin4
  N3: J2.pin5, J4.pin5

notes:
  blue:SCK
  green:CS
  yellow:DO
  white:PWM
