# Fritzing sketch zatu (saved by Fritzing 0.9.3b)
perfboards: 1

parts:
  Part1 = Arduino Uno (Rev3)  # not connected
  Q1 = Basic FET P-Channel [package="TO220 [THT]"]
  F1 = FUSE [package=fuse_5mm]
  R1 = Resistor [tolerance=±5% resistance=220 package=THT]
  C1 = Ceramic Capacitor [capacitance=100nF package="100 mil [THT, multilayer]"]  # not connected
  J1 = Screw terminal - 2 pins [package=THT]
  J2 = Screw terminal - 2 pins [package=THT]
  J3 = female pin header, 3 pins [form="♀ (female)"]
  J4 = female pin header, 3 pins [form="♀ (female)"]
  R2 = Resistor [tolerance=±5% resistance=220 package=THT]

nets:
  N1: Q1.gate, J1.pin1
  N2: Q1.source, J3.pin3
  N3: F1.2, J1.pin2
  N4: R1.Pin_1, J4.pin1
  N5: J2.pin2, R2.Pin_0
  N6: J3.pin1, R2.Pin_1
